# Fritzing sketch raincloud-wiring (saved by Fritzing 1.0.0)

parts:
  Arduino_Uno_R3 = Arduino Uno R3
  GY-906_/_MLX90614 = GY-906 / MLX90614
  Hydreon_RG-11 = Hydreon RG-11
  PC817_supply_monitor = PC817 supply monitor
  Regulated_12V = Regulated 12V
  Supply_fuse = Supply fuse
  2_2k_ohm_/_0_25W = 2.2k ohm / 0.25W
  D2_pullup_/_10k = D2 pullup / 10k
  D3_pullup_/_10k = D3 pullup / 10k
  D4_pullup_/_10k = D4 pullup / 10k

nets:
  5V: Arduino_Uno_R3.5V, GY-906_/_MLX90614.VIN, D2_pullup_/_10k.5V, D3_pullup_/_10k.5V, D4_pullup_/_10k.5V
  GND: Arduino_Uno_R3.GND, GY-906_/_MLX90614.GND, Hydreon_RG-11.COM, PC817_supply_monitor.E_/_GND
  N1: Arduino_Uno_R3.D2, Hydreon_RG-11.NC, D2_pullup_/_10k.D2
  N2: Arduino_Uno_R3.D3, Hydreon_RG-11.NO, D3_pullup_/_10k.D3
  N3: Arduino_Uno_R3.D4, PC817_supply_monitor.C_/_D4, D4_pullup_/_10k.D4
  N4: Arduino_Uno_R3.A4_/_SDA, GY-906_/_MLX90614.SDA
  N5: Arduino_Uno_R3.A5_/_SCL, GY-906_/_MLX90614.SCL
  N6: Hydreon_RG-11.PWR1_+12V, Supply_fuse.OUT, 2_2k_ohm_/_0_25W.1
  N7: Hydreon_RG-11.PWR2_return, PC817_supply_monitor.K_/_LED-, Regulated_12V.Return
  N8: PC817_supply_monitor.A_/_LED+, 2_2k_ohm_/_0_25W.2
  N9: Regulated_12V.+12V, Supply_fuse.IN

custom parts:
  Arduino Uno R3: Device-reference wiring part. Connect by labeled callouts, not physical pin positions. No PCB footprint. Photos: Hydreon and ProtoSupplies; Uno artwork: Fritzing CC BY-SA.
  GY-906 / MLX90614: Device-reference wiring part. Connect by labeled callouts, not physical pin positions. No PCB footprint. Photos: Hydreon and ProtoSupplies; Uno artwork: Fritzing CC BY-SA.
  Hydreon RG-11: Device-reference wiring part. Connect by labeled callouts, not physical pin positions. No PCB footprint. Photos: Hydreon and ProtoSupplies; Uno artwork: Fritzing CC BY-SA.
  PC817 supply monitor: Device-reference wiring part. Connect by labeled callouts, not physical pin positions. No PCB footprint. Photos: Hydreon and ProtoSupplies; Uno artwork: Fritzing CC BY-SA.
  Regulated 12V: Device-reference wiring part. Connect by labeled callouts, not physical pin positions. No PCB footprint. Photos: Hydreon and ProtoSupplies; Uno artwork: Fritzing CC BY-SA.
  Supply fuse: Device-reference wiring part. Connect by labeled callouts, not physical pin positions. No PCB footprint. Photos: Hydreon and ProtoSupplies; Uno artwork: Fritzing CC BY-SA.
  2.2k ohm / 0.25W: Device-reference wiring part. Connect by labeled callouts, not physical pin positions. No PCB footprint. Photos: Hydreon and ProtoSupplies; Uno artwork: Fritzing CC BY-SA.
  D2 pullup / 10k: Device-reference wiring part. Connect by labeled callouts, not physical pin positions. No PCB footprint. Photos: Hydreon and ProtoSupplies; Uno artwork: Fritzing CC BY-SA.
  D3 pullup / 10k: Device-reference wiring part. Connect by labeled callouts, not physical pin positions. No PCB footprint. Photos: Hydreon and ProtoSupplies; Uno artwork: Fritzing CC BY-SA.
  D4 pullup / 10k: Device-reference wiring part. Connect by labeled callouts, not physical pin positions. No PCB footprint. Photos: Hydreon and ProtoSupplies; Uno artwork: Fritzing CC BY-SA.
